# Fritzing sketch cerberus (saved by Fritzing 0.9.6b)
circuit board: 5.32161cm x 3.19475cm
breadboards: 1

parts:
  R2_150kΩ = Resistor [tolerance=±5% power=0.25 resistance=150k package=THT]
  R1_1MΩ = Resistor [tolerance=±5% power=0.25 resistance=1M package=THT]
  Raspberry_Pi = Raspberry Pi Header 40pin [form="♂ (male)" package=THT]
  ULN2003A = ULN2003A [package="DIP16 [THT]"]
  MCP3008 = MCP3008 [package=dil16]
  R5_1kΩ = Resistor [tolerance=±5% resistance=1k power=0.25 package=THT]
  R3_10Ω = Resistor [tolerance=±5% resistance=1.2 power=0.25 package=THT]
  R4_10Ω = Resistor [tolerance=±5% resistance=1.2 power=0.25 package=THT]
  CON = female pin header, 4 pins [form="♀ (female)"]
  LCD = female pin header, 2 pins [form="♀ (female)"]
  EXT = female pin header, 4 pins [form="♀ (female)"]

nets:
  N1: R2_150kΩ.Pin_0, R1_1MΩ.Pin_0, MCP3008.CH0
  N2: R2_150kΩ.Pin_1, Raspberry_Pi.GND, ULN2003A.0V, MCP3008.DGND, MCP3008.AGND, CON.pin2, LCD.pin1, EXT.pin2
  N3: R1_1MΩ.Pin_1, R3_10Ω.Pin_0, R4_10Ω.Pin_0, CON.pin1, EXT.pin1
  3V3: Raspberry_Pi.3v3, Raspberry_Pi.3V3, MCP3008.VREF, MCP3008.VDD
  N4: Raspberry_Pi.GIPO17, Raspberry_Pi.GIPO22
  N5: Raspberry_Pi.GIPO10, MCP3008.Din
  N6: Raspberry_Pi.GIPO9, MCP3008.Dout
  N7: Raspberry_Pi.GIPO11, MCP3008.CLK
  N8: Raspberry_Pi.GIPO8, MCP3008.CS/SHDN
  N9: Raspberry_Pi.GIPO25, R5_1kΩ.Pin_1
  N10: Raspberry_Pi.5V, LCD.pin2
  N11: ULN2003A.In_1, R5_1kΩ.Pin_0
  N12: ULN2003A.Out_1, R3_10Ω.Pin_1, R4_10Ω.Pin_1
  N13: CON.pin3, EXT.pin3
  N14: CON.pin4, EXT.pin4

notes:
  a
  b
  E
  P

custom parts:
  Raspberry Pi Header 40pin: Raspberry Pi 40 pin header - for creating your own shields.
